# Fritzing sketch Balance Bot (saved by Fritzing 1.0.5)
breadboards: 1

parts:
  M1 = gear-motor
  M2 = gear-motor
  Part2 = InvenSense MPU6050
  VCC1 = Battery block 9V [internal_resistance=0.1Ω]
  Part5 = Adafruit DRV8833 DC/Stepper Motor Driver [part_number="Adafruit #3297"]
  Part6 = ESP-WROOM-32 [ESP-32S] Module [part_number=ESP-WROOM-32]
  VCC3 = Battery [internal_resistance=0.1Ω]

nets:
  N1: M1.pin_1, Part5.AOUT2
  N2: M1.pin_2, Part5.AOUT1
  N3: M2.pin_1, Part5.BOUT1
  N4: M2.pin_2, Part5.BOUT2
  VCC: Part2.VCC, Part5.VMOTOR, Part6.3V3, VCC3.+
  GND: Part2.GND, VCC1.-, Part5.GND, Part6.GND, VCC3.-
  N5: Part2.SCL, Part6.IO22
  N6: Part2.SDA, Part6.IO21
  N7: Part2.INT, Part6.IO33
  N8: VCC1.+, Part5.PWRIN
  N9: Part5.BIN1, Part6.IO19
  N10: Part5.BIN2, Part6.IO18
  N11: Part5.AIN2, Part6.IO17
  N12: Part5.AIN1, Part6.IO16

custom parts:
  Adafruit DRV8833 DC/Stepper Motor Driver: Spin two DC motors or step one bi-polar or uni-polar stepper with up to 1.2A per channel using the DRV8833. This motor driver chip is a nice alternative to the TB6612 driver. Like that chip, you get 2 full H-bridges, but this chip is better for low voltage uses (can run from 2.7V up to 10.8V motor power) and has built in current limiting capability. We set it up for 1A current limiting so you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
  ESP-WROOM-32 [ESP-32S] Module: Espressif ESP-WROOM-32 WiFi/Bluetooth LE microcontroller module also known as the Ai-Thinker ESP-32S module with similar formfactor. The ESP32 is a microcontroller chip with WiFi and BLE capabilities. The chip is developed by Espressif and is the successor to the popular ESP8266 WiFi module.
