# Fritzing sketch Balance Bot (saved by Fritzing 1.0.5)
breadboards: 1

parts:
  M1 = gear-motor
  M2 = gear-motor
  Part5 = Adafruit DRV8833 DC/Stepper Motor Driver [part_number="Adafruit #3297"]
  VCC3 = Battery [internal_resistance=0.1Ω]
  VCC4 = Battery [internal_resistance=0.1Ω]
  VCC5 = Battery [internal_resistance=0.1Ω]
  Mod1 = Raspberry Pi Pico W
  MPU-1 = Adafruit MPU6050

nets:
  N1: M1.pin_1, Part5.AOUT2
  N2: M1.pin_2, Part5.AOUT1
  N3: M2.pin_1, Part5.BOUT1
  N4: M2.pin_2, Part5.BOUT2
  N5: Part5.PWRIN, VCC5.+
  GND: Part5.GND, VCC3.-, VCC4.-, Mod1.pin_38, Mod1.pin_42, MPU-1.GND
  N6: Part5.VMOTOR, VCC3.+, Mod1.pin_39, MPU-1.VCC
  N7: Part5.NFAULT, Mod1.pin_17
  N8: Part5.BIN1, Mod1.pin_16
  N9: Part5.BIN2, Mod1.pin_15
  N10: Part5.!SLEEP, Mod1.pin_14
  N11: Part5.AIN2, Mod1.pin_12
  N12: Part5.AIN1, Mod1.pin_11
  N13: VCC4.+, VCC5.-
  N14: Mod1.pin_29, MPU-1.INT
  N15: Mod1.pin_31, MPU-1.SDA
  N16: Mod1.pin_32, MPU-1.SCL

custom parts:
  Adafruit DRV8833 DC/Stepper Motor Driver: Spin two DC motors or step one bi-polar or uni-polar stepper with up to 1.2A per channel using the DRV8833. This motor driver chip is a nice alternative to the TB6612 driver. Like that chip, you get 2 full H-bridges, but this chip is better for low voltage uses (can run from 2.7V up to 10.8V motor power) and has built in current limiting capability. We set it up for 1A current limiting so you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
  Raspberry Pi Pico W: Raspberry Pi Pico W. Based around the RP2040 microcontroller the Pico W is a low cost microcontroller device bringing Raspberry Pi quality, cost, and easy of use to the microcontroller space. The areas marked KEEPOUT in pcb silkscreen should not have traces running through them to avoid shorts on a soldered in module!
  Adafruit MPU6050: The MPU-6050 is a popular six axis accelerometer and gyroscope (gyro) that has all the info you need on how things are shakin' and spinnin' . With six axes of sensing and 16-bit measurements, you'll have everything you need to give your robot friend an inner ear. This combination of gyroscopes and accelerometers is commonly referred to as an Inertial Measurement Unit or IMU. Not so long ago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
